// Logisim project multi.circ as structural Verilog
// MUX
module mux4_1 (
  input  A0,
  input  A1,
  input  D0,
  input  D1,
  input  D2,
  input  D3,
  output Y
);

  wire not_1_out, not_2_out, \И_2_out , \И_3_out , \И_4_out , \И_out ;

  not not_1 (not_1_out, A0);
  not not_2 (not_2_out, A1);
  and \u_И  (\И_out , not_1_out, not_2_out, D0);
  and \u_И_2  (\И_2_out , not_2_out, A0, D1);
  and \u_И_3  (\И_3_out , not_1_out, D2, A1);
  and \u_И_4  (\И_4_out , A0, D3, A1);
  or \u_ИЛИ  (Y, \И_out , \И_2_out , \И_3_out , \И_4_out );

  // Notes on the sheet:
  //   Мультиплексор
endmodule

module mux16_1 (
  input  D0,
  input  D1,
  input  D2,
  input  D3,
  input  D4,
  input  D5,
  input  D6,
  input  D7,
  input  D8,
  input  D9,
  input  D10,
  input  D11,
  input  D12,
  input  D13,
  input  D14,
  input  D15,
  input  A0,
  input  A1,
  input  A2,
  input  A3,
  output Y
);

  wire mux4_1_1_y, mux4_1_2_y, mux4_1_3_y, mux4_1_4_y;

  mux4_1 mux4_1_1 (.A0(A0), .A1(A1), .D0(D0), .D1(D1), .D2(D2), .D3(D3), .Y(mux4_1_1_y));
  mux4_1 mux4_1_2 (.A0(A0), .A1(A1), .D0(D4), .D1(D5), .D2(D6), .D3(D7), .Y(mux4_1_2_y));
  mux4_1 mux4_1_3 (.A0(A0), .A1(A1), .D0(D8), .D1(D9), .D2(D10), .D3(D11), .Y(mux4_1_3_y));
  mux4_1 mux4_1_4 (.A0(A0), .A1(A1), .D0(D12), .D1(D13), .D2(D14), .D3(D15), .Y(mux4_1_4_y));
  mux4_1 mux4_1_5 (.A0(A2), .A1(A3), .D0(mux4_1_1_y), .D1(mux4_1_2_y), .D2(mux4_1_3_y), .D3(mux4_1_4_y), .Y(Y));
endmodule

module dmux1_4 (
  input  D1,
  input  A1,
  input  A0,
  output Y3,
  output Y2,
  output Y1,
  output Y0
);

  wire and_1_out, and_2_out, and_5_out, and_6_out, deshif_1_a, deshif_1_b, deshif_1_c, deshif_1_d,
       deshif_1_e, deshif_1_f, deshif_1_g, not_1_out, not_2_out, not_3_out, not_4_out;

  and and_1 (and_1_out, D1, A1);
  and and_2 (and_2_out, D1, A1);
  not not_1 (not_1_out, A0);
  not not_2 (not_2_out, A1);
  not not_3 (not_3_out, A1);
  and and_3 (Y3, and_1_out, A0);
  and and_4 (Y2, and_2_out, not_1_out);
  and and_5 (and_5_out, D1, not_2_out);
  and and_6 (and_6_out, D1, not_3_out);
  not not_4 (not_4_out, A0);
  and and_7 (Y1, and_5_out, A0);
  and and_8 (Y0, and_6_out, not_4_out);
  deshif deshif_1 (
    .A3(Y3), .A2(Y2), .A1(Y1), .A0(Y0), .g(deshif_1_g), .f(deshif_1_f), .e(deshif_1_e), .d(deshif_1_d),
    .c(deshif_1_c), .b(deshif_1_b), .a(deshif_1_a));
  _7_Segment_Display u_7_segment_display_1 (
    .g(deshif_1_g), .f(deshif_1_f), .a(deshif_1_a), .b(deshif_1_b), .e(deshif_1_e), .d(deshif_1_d),
    .c(deshif_1_c));  // open: dp
endmodule

module deshif (
  input  A3,
  input  A2,
  input  A1,
  input  A0,
  output g,
  output f,
  output e,
  output d,
  output c,
  output b,
  output a
);

  wire and_1_out, and_2_out, and_3_out, and_4_out, and_5_out, and_6_out, and_7_out, and_8_out, and_9_out,
       and_10_out, and_11_out, and_12_out, and_13_out, and_14_out, and_15_out, and_16_out, and_17_out,
       and_18_out, and_19_out, and_20_out, and_21_out, and_22_out, and_23_out, and_24_out, and_25_out,
       and_26_out, not_1_out, not_2_out, not_3_out, not_4_out, not_5_out, not_6_out, not_7_out, not_8_out,
       not_9_out, not_10_out, not_11_out, not_12_out, not_13_out, not_14_out, not_15_out, not_16_out,
       not_17_out, not_18_out, not_19_out, not_20_out, not_21_out, not_22_out, not_23_out, not_24_out,
       not_25_out, not_26_out, not_27_out, not_28_out, not_29_out, not_30_out, not_31_out, not_32_out,
       not_33_out, not_34_out, not_35_out, not_36_out, not_37_out, not_38_out, not_39_out, not_40_out,
       not_41_out, not_42_out, not_43_out, not_44_out, not_45_out, not_46_out, not_47_out, not_48_out,
       not_49_out, not_50_out, not_51_out, not_52_out;

  not not_1 (not_1_out, A3);
  and and_1 (and_1_out, not_1_out, not_2_out, A1);
  not not_2 (not_2_out, A2);
  not not_3 (not_3_out, A3);
  and and_2 (and_2_out, not_3_out, A2, not_4_out);
  not not_4 (not_4_out, A1);
  not not_5 (not_5_out, A3);
  and and_3 (and_3_out, not_5_out, A2, not_6_out);
  not not_6 (not_6_out, A0);
  and and_4 (and_4_out, A3, not_7_out, not_8_out);
  not not_7 (not_7_out, A2);
  not not_8 (not_8_out, A1);
  not not_9 (not_9_out, A3);
  not not_10 (not_10_out, A1);
  and and_5 (and_5_out, not_9_out, not_10_out, not_11_out);
  not not_11 (not_11_out, A0);
  not not_12 (not_12_out, A3);
  and and_6 (and_6_out, not_12_out, A2, not_13_out);
  not not_13 (not_13_out, A1);
  not not_14 (not_14_out, A3);
  and and_7 (and_7_out, not_14_out, A2, not_15_out);
  not not_15 (not_15_out, A0);
  not not_16 (not_16_out, A2);
  and and_8 (and_8_out, A3, not_16_out, not_17_out);
  not not_17 (not_17_out, A1);
  not not_18 (not_18_out, A2);
  not not_19 (not_19_out, A1);
  and and_9 (and_9_out, not_18_out, not_19_out, not_20_out);
  not not_20 (not_20_out, A0);
  not not_21 (not_21_out, A3);
  and and_10 (and_10_out, not_21_out, A1, not_22_out);
  not not_22 (not_22_out, A0);
  not not_23 (not_23_out, A3);
  not not_24 (not_24_out, A2);
  not not_25 (not_25_out, A0);
  not not_26 (not_26_out, A3);
  not not_27 (not_27_out, A2);
  not not_28 (not_28_out, A3);
  not not_29 (not_29_out, A0);
  not not_30 (not_30_out, A3);
  not not_31 (not_31_out, A1);
  not not_32 (not_32_out, A2);
  not not_33 (not_33_out, A1);
  not not_34 (not_34_out, A2);
  and and_11 (and_11_out, not_34_out, not_35_out);
  not not_35 (not_35_out, A1);
  not not_36 (not_36_out, A3);
  and and_12 (and_12_out, not_36_out, A0);
  not not_37 (not_37_out, A3);
  and and_13 (and_13_out, not_37_out, A2);
  not not_38 (not_38_out, A3);
  and and_14 (and_14_out, not_38_out, not_39_out);
  not not_39 (not_39_out, A2);
  not not_40 (not_40_out, A3);
  not not_41 (not_41_out, A1);
  and and_15 (and_15_out, not_40_out, not_41_out, not_42_out);
  not not_42 (not_42_out, A0);
  not not_43 (not_43_out, A2);
  and and_16 (and_16_out, not_43_out, not_44_out);
  not not_44 (not_44_out, A1);
  not not_45 (not_45_out, A3);
  and and_17 (and_17_out, not_45_out, A1, A0);
  not not_46 (not_46_out, A3);
  not not_47 (not_47_out, A2);
  and and_18 (and_18_out, not_46_out, not_47_out, not_48_out);
  not not_48 (not_48_out, A0);
  not not_49 (not_49_out, A3);
  and and_19 (and_19_out, not_49_out, A1);
  not not_50 (not_50_out, A3);
  and and_20 (and_20_out, not_50_out, A2, A0);
  not not_51 (not_51_out, A2);
  and and_21 (and_21_out, A3, not_51_out, not_52_out);
  not not_52 (not_52_out, A1);
  or or_1 (g, and_1_out, and_2_out, and_3_out, and_4_out);
  or or_2 (f, and_5_out, and_6_out, and_7_out, and_8_out);
  or or_3 (e, and_9_out, and_10_out);
  and and_22 (and_22_out, not_23_out, not_24_out, not_25_out);
  and and_23 (and_23_out, not_26_out, not_27_out, A1);
  and and_24 (and_24_out, not_28_out, A1, not_29_out);
  and and_25 (and_25_out, not_30_out, A2, not_31_out, A0);
  and and_26 (and_26_out, A3, not_32_out, not_33_out);
  or or_4 (c, and_11_out, and_12_out, and_13_out);
  or or_5 (b, and_14_out, and_15_out, and_16_out, and_17_out);
  or or_6 (a, and_18_out, and_19_out, and_20_out, and_21_out);
  or or_7 (d, and_22_out, and_23_out, and_24_out, and_25_out, and_26_out);
endmodule
